# Fritzing sketch Stromverbrauchsmessung (saved by Fritzing 1.0.3b)
breadboards: 1

parts:
  LCD1 = LCD screen  # not connected
  Mod1 = Raspberry Pi Pico W
  Mod2 = KY-018 Photoresistor Module [package="Breakout board"]

nets:
  N1: Mod1.pin_3, Mod1.pin_8, Mod1.pin_13, Mod1.pin_18, Mod1.pin_23, Mod1.pin_26, Mod1.pin_27, Mod1.pin_28, Mod1.pin_33, Mod1.pin_38, Mod1.pin_40, Mod1.pin_42, Mod2.-
  N2: Mod1.pin_20, Mod2.S
  N3: Mod1.pin_36, Mod2.Vin

notes:
  KY-018

custom parts:
  Raspberry Pi Pico W: Raspberry Pi Pico W. Based around the RP2040 microcontroller the Pico W is a low cost microcontroller device bringing Raspberry Pi quality, cost, and easy of use to the microcontroller space. The areas marked KEEPOUT in pcb silkscreen should not have traces running through them to avoid shorts on a soldered in module!
  KY-018 Photoresistor Module: KY-018 Photoresistor module, used to measure light intensity. It can determine the presence or absence of light.
